# Fritzing sketch Sorting-Hat (saved by Fritzing 0.9.3b)
breadboards: 1

parts:
  S1 = Pushbutton [package="[THT]"]
  LED1 = LED - 5mm [color="Red (633nm)" package="5 mm [THT]"]
  LED2 = LED - 5mm [color="Green (555nm)" package="5 mm [THT]"]
  LED3 = LED - 5mm [color="Blue (470nm)" package="5 mm [THT]"]
  LED4 = LED - 5mm [color="Yellow (585nm)" package="5 mm [THT]"]
  R1 = Resistor [tolerance=±5% resistance=220 package=THT]
  R2 = Resistor [tolerance=±5% resistance=220 package=THT]
  R3 = Resistor [tolerance=±5% resistance=220 package=THT]
  R4 = Resistor [tolerance=±5% resistance=220 package=THT]
  Raspberry_Pi_1 = Raspberry Pi 3 [part_number=RPI-3-V1.2]

nets:
  N1: S1.Pin_1, S1.Pin_2, Raspberry_Pi_1.GIPO22
  N2: S1.Pin_3, S1.Pin_4, R1.Pin_1, R2.Pin_1, R3.Pin_1, R4.Pin_1, Raspberry_Pi_1.GND
  N3: LED1.cathode, R1.Pin_0
  N4: LED1.anode, Raspberry_Pi_1.GPIO2
  N5: LED2.cathode, R2.Pin_0
  N6: LED2.anode, Raspberry_Pi_1.GPIO3
  N7: LED3.cathode, R4.Pin_0
  N8: LED3.anode, Raspberry_Pi_1.GIPO17
  N9: LED4.cathode, R3.Pin_0
  N10: LED4.anode, Raspberry_Pi_1.GIPO27
